# Fritzing sketch SensorBMP280 (saved by Fritzing 0.9.3b)
circuit board: 6.88566cm x 5.36311cm
breadboards: 1

parts:
  R7 = Resistor [tolerance=±5% resistance=220 package=THT]
  R8 = Resistor [tolerance=±5% resistance=220 package=THT]
  R9 = Resistor [tolerance=±5% resistance=220 package=THT]
  R10 = Resistor [tolerance=±5% resistance=220 package=THT]
  LED7 = LED - 5mm [color="Blue (525nm)" package="5 mm [THT]"]
  LED8 = LED - 5mm [color="Yellow (595nm)" package="5 mm [THT]"]
  LED9 = LED - 5mm [color="Green (570nm)" package="5 mm [THT]"]
  LED10 = LED - 5mm [color="Red (633nm)" package="5 mm [THT]"]
  Arduino1 = Arduino Uno (Rev3)
  Componente1 = Adafruit_BMP280

nets:
  GND: R7.Pin_0, R8.Pin_0, R9.Pin_0, R10.Pin_0, Arduino1.GND, Componente1.GND
  N1: R7.Pin_1, LED7.cathode
  N2: R8.Pin_1, LED8.cathode
  N3: R9.Pin_1, LED9.cathode
  N4: R10.Pin_1, LED10.cathode
  N5: LED7.anode, Arduino1.D7
  N6: LED8.anode, Arduino1.D6_PWM
  N7: LED9.anode, Arduino1.D5_PWM
  N8: LED10.anode, Arduino1.D4
  N9: Arduino1.D10_PWM/SS, Componente1.CS
  N10: Arduino1.D11_PWM/MOSI, Componente1.SDI/SDA
  N11: Arduino1.D12/MISO, Componente1.SDO/ADR
  N12: Arduino1.D13/SCK, Componente1.SCK/SCL
  3V3: Arduino1.3V3, Componente1.3.3V

custom parts:
  Adafruit_BMP280: Bosch has stepped up their game with their new BMP280 sensor, an environmental sensor with temperature, barometric pressure that is the next generation upgrade to the BMP085/BMP180/BMP183. This sensor is great for all sorts of weather sensing and can even be used in both I2C and SPI! This precision sensor from Bosch is the best low-cost, precision sensing solution for measuring barometric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

// code stored in the sketch: TemperaturSensorLM35.ino
/* 
 * Fisica Aplicada a Computacao - Engenharia Informatica
 * Aluno: Hugo Alexandre, Tiago Filipe, Omar Pizon
 * Mestre: Nuno Pereira
 * 2018-19
 * Hardware: Arduino Uno R3
 * Descricao: testa estruturas de programacao, sensor de temperatura.
 * Primeiro trabalho em sala de aula.
 * Versão 20/02/2019
 * Recursos: https://www.arduino.cc/en/Reference/FunctionDeclaration
 *           https://www.arduino.cc/en/Reference/If
 *           https://www.arduino.cc/en/Reference/For
 *           https://www.arduino.cc/en/Reference/SwitchCase
 *           https://www.arduino.cc/en/Reference/While
 *           https://www.arduino.cc/en/Reference/DoWhile
 *           https://www.arduino.cc/en/Reference/Break
 *           https://www.arduino.cc/en/Reference/Continue
 *           https://www.arduino.cc/en/Reference/Return
*/


//variáveis globais que irão mostrar os valores dos sensores e utilização durante a execução do trabalho;
byte Vcc = 11;
byte Trig = 12;
byte Echo = 13;
float distance;               // variavel para receber valor de distancia;
byte triggerDuration = 10;          // us, "conforme citação do mestre nuno e unidade de medida;
unsigned int sampleDelay = 10;      // ms, "conforme citação do mestre nuno e unidade de medida;
unsigned int timeout = 23530;             // tempo correspondente a d > 4m, "conforme citação do mestre nuno e unidade de medida;

//escolhemos a variavél float por receber números decimais que ocupam 32 bits(4 bytes);
//assim não precesariamos usar a variavel double que ocupa o dobro em alguns casos, economizando até mesmo no espaço de memoria;
//essas variaveis podem tomar valores entre -3.4028235E+38 e +3.4028235E+38.

float duration_a = 0.;     // "conforme citação do mestre nuno e unidade de medida. nome variavel. recebe duração;
float distance_a = 0.;
float duration_suav = 0.;   // "conforme citação do mestre nuno e unidade de medida. nome variavel. recebe suavização duração;
float distance_suav = 0.;   // "conforme citação do mestre nuno e unidade de medida. nome variavel. recebe suavização distancia;
int contador = 0;           // contador usado para as formulas, contagem das medições. ideia baseada do primeiro trabalho FAC;
const int valor_media = 3;    // contador usado para as formulas, contagem das medições deslizante, ideia baseada do primeiro trabalho FAC;
const float suavizacao = 0.3; // suavização usado para as formulas, ideia baseada do primeiro trabalho FAC;
float media_a = 0.;           //variavel para medias em geral;
float media_b = 0.;           //variavel para medias em geral;
float duration_media = 0.;    //variavel para media da duração;
float distance_media = 0.;    //variavel para media da distancia;
float duration_mmm = 0.;      //variavel para media acumulativa;
float distance_mmm = 0.;    //variavel para media acumulativa;
float duration_array[valor_media];    //array para valores de duração, ideia baseada do primeiro trabalho FAC;;
float distance_array[valor_media];    //array para valores de distancia, ideia baseada do primeiro trabalho FAC;;


//após a formulação do calculo os acendimentos dos led ocorreram nos seguintes pinos;
//assim como ocorre no trabalho 1 descritivo ao qual utilizamos como base e ideia para as formulas.

 
  const int pino7 = 7; //byte pino7 = 7;
  const int pino6 = 6; //byte pino6 = 6;
  const int pino5 = 5; //byte pino5 = 5;
  const int pino4 = 4; //byte pino4 = 4;
  

//#define ultrasom
    //#define mms
    //#define mmc
    //#define mmm
    //#define mmd
    //#define mserial
    //#define mplotter
    //#define gnuplot
    
#ifdef ultrasom

// Initialization
void setup() {
  pinMode(Vcc, OUTPUT);
  pinMode(Trig, OUTPUT);
  pinMode(Echo, INPUT);
  digitalWrite(Vcc, HIGH);
  digitalWrite(Trig, LOW);
  Serial.begin(9600);
  while(!Serial);
}
// Main loop
void loop() {
  delay(sampleDelay);
  digitalWrite(Trig, HIGH);
  delayMicroseconds(triggerDuration);
  digitalWrite(Trig, LOW);
  unsigned long duration = pulseIn(Echo, HIGH, timeout);
  distance = (float)duration/58.8;

#ifdef mmm
  duration_array[contador]=duration;
  distance_array[contador]=distance;
  contador++;
if(contador == valor_media) {
  duration_media = 0.;
  distance_media = 0.;
for(int k = 0; k < valor_media; k++){
  duration_media=duration_media + duration_array[k];
  distance_media=distance_media + distance_array[k];
}
  duration_media=duration_media / valor_media;
  distance_media=distance_media / valor_media;
  contador = 0;
}
#endif mmm
 
#ifdef mms  // inicio dos calculos das ações de suavização;
  duration_a = duration_suav;
  distance_a = distance_suav;
  duration_suav = duration + (duration_a - duration) * suavizacao;
  distance_suav = distance + (distance_a - distance) * suavizacao;
#endif mms

#ifdef mmc  // inicio do calculos das media correntes ou acumulativas
  contador++;
  duration_mmm += duration;
  distance_mmm += distance;
  duration_media = duration_mmm / contador;
  distance_media = distance_mmm / contador;
#endif mmc

#ifdef mmd  //inicio da ação de calculo das medias deslizantes;
if(contador < valor_media) {
    duration_array[contador]=duration;
    distance_array[contador]=distance;
    contador++;
}
if(contador == valor_media) {  // baseado no descritivo do quadro do mestre nuno, esta formula, 
for(int k = 0; k < valor_media; k++){   //efetua a troca dos valores dos array e traz novas medições trocando a mais antiga;
   if(k < (valor_media - 1)){
     duration_array[k]=duration_array[k + 1];
     distance_array[k]=distance_array[k + 1];
} else {
     duration_array[k]=duration;
     distance_array[k]=distance;
}
}
for(int k = 0; k < valor_media; k++){                   // dentro das medias ja calculadas e armazenadas no array, 
    duration_media=duration_media + duration_array[k];    //iremos receber novo valor de duração medida e armazenar dentro de um array e 
    distance_media=distance_media + distance_array[k];    //utilizar para efetuar o calculo de nova media com valores atualizados;
}
    duration_media=duration_media / valor_media;
    distance_media=distance_media / valor_media;
}
#endif mmd

#ifdef gnuplot
  Serial.print(F("#Fisica Aplicada Computação | 2018-19"));
  Serial.print(F("#Duration (us)\tDistance (cm)"));
  Serial.print(F("\tSuavização duration (us)\tSuavização distance (cm)"));
  Serial.println(F("\tMedia duration (us)\tMedia distance (cm)"));
#endif gnuplot

#ifdef mplotter
  Serial.print(F("\tSuavização duration(us): "));
  Serial.print(duration_suav);          //imprimi a suavização da duração;
  Serial.print(F("\tSuavização distance(us): "));
  Serial.print(distance_suav);         //imprimi a suavização da distancia;
  Serial.print(F("\tDuration(us): "));
  Serial.print(duration);               //imprimi a duração, "conforme citação do mestre nuno e unidade de medida. nome variavel. recebe duração;
  Serial.print(F("\tDistance(cm): "));
  Serial.println(distance);     //imprimi a distancia, "conforme citação do mestre nuno e unidade de medida. nome variavel. recebe distancia;
#endif mplotter

#ifdef mserial
  Serial.print(F("\tMedia duration(us): "));
  Serial.print(duration_media);             //imprimi a media da duração, media final;
  Serial.print(F("\tMedia distance(cm): "));
  Serial.print(distance_media);           //imprimi a media da distancia, media final;
  Serial.print(F("\tDuration(us): "));
  Serial.print(duration);               //imprimi a duração, "conforme citação do mestre nuno e unidade de medida. nome variavel. recebe duração;
  Serial.print(F("\tDistance(cm): "));
  Serial.println(distance);     //imprimi a distancia, "conforme citação do mestre nuno e unidade de medida. nome variavel. recebe distancia;
  
if (duration > 0 && duration <= 9000){
   digitalWrite(pino7, HIGH);          // para os valores de if luz de led acessa, estará HIGH;
   Serial.print(F("LED Blue  "));
}
if (duration > 9000 && duration <= 55000){
   digitalWrite(pino6, HIGH);      // para os valores de if luz de led acessa, estará HIGH;
   Serial.print(F("LED Yellow  "));
}
if (distance > 0 && distance <= 1900){
   digitalWrite(pino5, HIGH);     // para os valores de if luz de led acessa, estará HIGH;
   Serial.print(F("LED Green  "));
}
if (distance > 1900 && distance <= 4100){
   digitalWrite(pino4, HIGH);         // para os valores de if luz de led acessa, estará HIGH;
   Serial.print(F("LED Red  "));
}
#endif mserial
}

#endif ultrasom
