# Fritzing sketch TemperaturSensorDHT11 (saved by Fritzing 0.9.3b)
circuit board: 6.88566cm x 5.36311cm
breadboards: 1

parts:
  R7 = Resistor [tolerance=±5% resistance=220 package=THT]
  R8 = Resistor [tolerance=±5% resistance=220 package=THT]
  R9 = Resistor [tolerance=±5% resistance=220 package=THT]
  R10 = Resistor [tolerance=±5% resistance=220 package=THT]
  LED7 = LED - 5mm [color="Blue (525nm)" package="5 mm [THT]"]
  LED8 = LED - 5mm [color="Yellow (595nm)" package="5 mm [THT]"]
  LED9 = LED - 5mm [color="Green (570nm)" package="5 mm [THT]"]
  LED10 = LED - 5mm [color="Red (633nm)" package="5 mm [THT]"]
  R12 = Resistor [tolerance=±10% resistance=4.7 package=THT]
  Arduino1 = Arduino Uno (Rev3)
  DHT1 = DHT11 Humitidy and Temperature Sensor

nets:
  GND: R7.Pin_0, R8.Pin_0, R9.Pin_0, R10.Pin_0, R12.Pin_0, Arduino1.GND, DHT1.GND
  N1: R7.Pin_1, LED7.cathode
  N2: R8.Pin_1, LED8.cathode
  N3: R9.Pin_1, LED9.cathode
  N4: R10.Pin_1, LED10.cathode
  N5: LED7.anode, Arduino1.D7
  N6: LED8.anode, Arduino1.D6_PWM
  N7: LED9.anode, Arduino1.D5_PWM
  N8: LED10.anode, Arduino1.D4
  N9: Arduino1.D2, DHT1.VDD
  N10: Arduino1.5V, DHT1.DATA

custom parts:
  DHT11 Humitidy and Temperature Sensor: DHT11 Humidity and Temperature Sensor

// code stored in the sketch: TemperaturSensorLM35.ino
/* 
 * Fisica Aplicada a Computacao - Engenharia Informatica
 * Aluno: Hugo Alexandre, Tiago Filipe, Omar Pizon
 * Mestre: Nuno Pereira
 * 2018-19
 * Hardware: Arduino Uno R3
 * Descricao: testa estruturas de programacao, sensor de temperatura.
 * Primeiro trabalho em sala de aula.
 * Versão 20/02/2019
 * Recursos: https://www.arduino.cc/en/Reference/FunctionDeclaration
 *           https://www.arduino.cc/en/Reference/If
 *           https://www.arduino.cc/en/Reference/For
 *           https://www.arduino.cc/en/Reference/SwitchCase
 *           https://www.arduino.cc/en/Reference/While
 *           https://www.arduino.cc/en/Reference/DoWhile
 *           https://www.arduino.cc/en/Reference/Break
 *           https://www.arduino.cc/en/Reference/Continue
 *           https://www.arduino.cc/en/Reference/Return
*/


//variáveis globais que irão mostrar os valores dos sensores e utilização durante a execução do trabalho;
byte Vcc = 11;
byte Trig = 12;
byte Echo = 13;
float distance;               // variavel para receber valor de distancia;
byte triggerDuration = 10;          // us, "conforme citação do mestre nuno e unidade de medida;
unsigned int sampleDelay = 10;      // ms, "conforme citação do mestre nuno e unidade de medida;
unsigned int timeout = 23530;             // tempo correspondente a d > 4m, "conforme citação do mestre nuno e unidade de medida;

//escolhemos a variavél float por receber números decimais que ocupam 32 bits(4 bytes);
//assim não precesariamos usar a variavel double que ocupa o dobro em alguns casos, economizando até mesmo no espaço de memoria;
//essas variaveis podem tomar valores entre -3.4028235E+38 e +3.4028235E+38.

float duration_a = 0.;     // "conforme citação do mestre nuno e unidade de medida. nome variavel. recebe duração;
float distance_a = 0.;
float duration_suav = 0.;   // "conforme citação do mestre nuno e unidade de medida. nome variavel. recebe suavização duração;
float distance_suav = 0.;   // "conforme citação do mestre nuno e unidade de medida. nome variavel. recebe suavização distancia;
int contador = 0;           // contador usado para as formulas, contagem das medições. ideia baseada do primeiro trabalho FAC;
const int valor_media = 3;    // contador usado para as formulas, contagem das medições deslizante, ideia baseada do primeiro trabalho FAC;
const float suavizacao = 0.3; // suavização usado para as formulas, ideia baseada do primeiro trabalho FAC;
float media_a = 0.;           //variavel para medias em geral;
float media_b = 0.;           //variavel para medias em geral;
float duration_media = 0.;    //variavel para media da duração;
float distance_media = 0.;    //variavel para media da distancia;
float duration_mmm = 0.;      //variavel para media acumulativa;
float distance_mmm = 0.;    //variavel para media acumulativa;
float duration_array[valor_media];    //array para valores de duração, ideia baseada do primeiro trabalho FAC;;
float distance_array[valor_media];    //array para valores de distancia, ideia baseada do primeiro trabalho FAC;;


//após a formulação do calculo os acendimentos dos led ocorreram nos seguintes pinos;
//assim como ocorre no trabalho 1 descritivo ao qual utilizamos como base e ideia para as formulas.

 
  const int pino7 = 7; //byte pino7 = 7;
  const int pino6 = 6; //byte pino6 = 6;
  const int pino5 = 5; //byte pino5 = 5;
  const int pino4 = 4; //byte pino4 = 4;
  
    
//#define humidade
    //#define mms_humidade
    //#define mmc_humidade
    //#define mmm_humidade
    //#define mmd_humidade
    //#define mserial_humidade
    //#define mplotter_humidade


#ifdef humidade

#include "DHT.h"
// Declaration of global variables
byte DHTpin = 2;        // Digital pin to connect pin 2 of the sensor 
int delaySample = 200; // delay between measurements in ms
// Definition of the sensor
DHT dht(DHTpin, DHT11);
// Initialization 
void setup() {
  Serial.begin(115200); // Start serial port communications
  Serial.println(F("Fisica Aplicada Computação - EI (v1.0) | 2018-19\nDHT11 test\n"));
  dht.begin();  // Initialize sensor
  delay(delaySample); 
  }
// Main loop 
  void loop() {   
  delay(delaySample);
  float h = dht.readHumidity();     // Read relative humidity   
  float t = dht.readTemperature();  // Read temperature in Celcius   
  // Check validity of readings   
  if (isnan(h) || isnan(t)) {
    Serial.println(F("Invalid Data!"));
    return;   // Loops to the reading instructions without printing data   
    }

#ifdef mms_humidade
    duration_a = duration_suav;
    distance_a = distance_suav;
    duration_suav = h + (duration_a - h) * suavizacao;
    distance_suav = t + (distance_a - t) * suavizacao;
#endif mms_humidade

#ifdef mmm_humidade
  duration_array[contador] = h;
  distance_array[contador] = t;
  contador++;
if(contador == valor_media) {
  duration_media = 0.;
  distance_media = 0.;
for(int k = 0; k < valor_media; k++){
  duration_media=duration_media + duration_array[k];
  distance_media=distance_media + distance_array[k];
}
  duration_media=duration_media / valor_media;
  distance_media=distance_media / valor_media;
  contador = 0;
}
#endif mmm_humidade
 
#ifdef mmc_humidade // inicio do calculos das media correntes ou acumulativas
  contador++;
  duration_mmm += h;
  distance_mmm += t;
  duration_media = duration_mmm / contador;
  distance_media = distance_mmm / contador;
#endif mmc_humidade

#ifdef mmd_humidade  //inicio da ação de calculo das medias deslizantes;
if(contador < valor_media) {
    duration_array[contador] = h;
    distance_array[contador] = t;
    contador++;
}
if(contador == valor_media) {  // baseado no descritivo do quadro do mestre nuno, esta formula, 
for(int k = 0; k < valor_media; k++){   //efetua a troca dos valores dos array e traz novas medições trocando a mais antiga;
   if(k < (valor_media - 1)){
     duration_array[k]=duration_array[k + 1];
     distance_array[k]=distance_array[k + 1];
} else {
     duration_array[k] = h;
     distance_array[k] = t;
}
}
for(int k = 0; k < valor_media; k++){                   // dentro das medias ja calculadas e armazenadas no array, 
    duration_media=duration_media + duration_array[k];    //iremos receber novo valor de duração medida e armazenar dentro de um array e 
    distance_media=distance_media + distance_array[k];    //utilizar para efetuar o calculo de nova media com valores atualizados;
}
    duration_media=duration_media / valor_media;
    distance_media=distance_media / valor_media;
}
#endif mmd_humidade
