# Fritzing sketch Untitled Sketch 2 (saved by Fritzing 0.9.3b)
circuit board: 8.46667cm x 5.64444cm
breadboards: 1

parts:
  Componente1 = Arduino Uno (Rev3)
  LED1 = LED - 5mm [color="Blue (525nm)" package="5 mm [THT]"]
  LED5 = LED - 5mm [color="Orange (620nm)" package="5 mm [THT]"]
  LED7 = LED - 5mm [color="Green (555nm)" package="5 mm [THT]"]
  T1 = LM35 Temperature Sensor [thermistor_type=NTC package="TO92 [THT]"]
  LED8 = LED - 5mm [color="Infrared (850nm)" package="5 mm [THT]"]
  R2 = Resistor [tolerance=±5% resistance=220 package=THT]
  R5 = Resistor [tolerance=±5% resistance=220 package=THT]
  R6 = Resistor [tolerance=±5% resistance=220 package=THT]
  R7 = Resistor [tolerance=±5% resistance=220 package=THT]
  R8 = Resistor [tolerance=±5% resistance=220 package=THT]

nets (from the schematic view):
  N1: Componente1.A2, T1.Vout
  N2: Componente1.GND, R5.Pin_1, R7.Pin_0
  N3: Componente1.D4, Componente1.D5_PWM, LED1.cathode, LED5.cathode, LED5.anode, LED7.anode, R2.Pin_0, R2.Pin_1, R6.Pin_0, R6.Pin_1
  N4: Componente1.D6_PWM, R7.Pin_1
  N5: Componente1.D7, R8.Pin_1
  N6: Componente1.5V, T1.+Vs
  N7: LED7.cathode, LED8.cathode
  N8: T1.GND, R5.Pin_0
  N9: LED8.anode, R8.Pin_0

// code stored in the sketch: fritzing1.ino
 int sensor = 2;

  const int pino4; 
  const int pino5;
  const int pino6;
	const int pino7;

  float t = 0;
  float y = 0;
  float tmin = -40;
  float tmax = 120;
  float w = 1;
  float k = 0;
  float r = 0;


  void setup() {

  Serial.begin(9600);
  pinMode(sensor, INPUT); 
  randomSeed(analogRead(1)); 
       } 

  void loop() {

 delay(10);

 float ruido = 1 * random(-10,10); // calculo para o ruido;
      t = (float) millis()/1000.;; // acrescenta o calculo/contagem em millis;
      y = calculation (temp);
      temp = (func(y) + ruido);
      float leitura[3] = {temp};  // quantidade de valores guardado da temperatura;
      float leitura_a = 0;  // armazena valores da leitura atual;
      float media = 0;  // recebe a média;
      leitura_a += leitura[0]+leitura[1]+leitura[2];     // adicionar leitura atual a leituras; 

if (temp !=500){
      contador++;                    // variavel utilizada na função e calculo da media;contador para saber por quanto deve se dividir a soma da temperatura acumulada;
}
      media += leitura_a/contador;       // recebe o somatorio da próxima temperatura + temperatura atual e divide pelo contador;

#ifdef mmmedia  
     float mmm = leitura_a/3; 
#endif mmmedia

#ifdef suav   
      float mms = leitura[0] + (leitura[2] - leitura[0])*0.25; //suavização     
#endif suav

#ifdef mplotter
       Serial.print(F("  T0 = "  ));
       Serial.print(10); // marcação da linha de valor aleatorio da tempertura;
       Serial.print(F("  T1 = "  ));
       Serial.print(80); // marcação da linha de valor aleatorio da tempertura;
       Serial.print(F(" MMM = "));
       Serial.print(mmm);
       Serial.print(F(" Media = "));
       Serial.print(media);
       Serial.print(F("  Tmax = "  ));
       Serial.print(120);// marcação da linha de maior temperatura;
       Serial.print(F("  Tmin = "  ));
       Serial.print(-40); // marcação da linha de menor temperatura;
       Serial.print(F("  t = ")); //imprima na tela o resultado da função completa;
       Serial.println(temp);
#endif mplotter

#ifdef mserial
        Serial.print(F("\tT0= "));
        Serial.print(10); // marcação da linha de valor aleatorio da tempertura;
        Serial.print(F("\tT1= "));
        Serial.print(80); // marcação da linha de valor aleatorio da tempertura;
        Serial.print(F("\tt= "));     //imprima na tela a função completa;
        Serial.println(temp);
        Serial.print(F("\tTmin= "));
        Serial.print(-40); // marcação da linha de menor temperatura;
        Serial.print(F("\tTmax= "));
        Serial.print(120);// marcação da linha de maior temperatura;
        Serial.print(F("\tT= "));   //imprimi o resultado T com millis;
        Serial.print(t,2);
        Serial.print(F("\tContador= "));  
        Serial.print(contador);                 // imprimi a contagem;
        Serial.print(F("\tMedia= "));
        Serial.print(media);                 // imprimi media mcm;
        Serial.print(F("\tMMM= "));
        Serial.print(mmm);   // imprimi media mmm;
        Serial.print(F("\tMMS= "));
        Serial.print(mms);     // imprimi media mmm;
//Condição para resultados de temperaturas, com seleção dos pinos escolhidos e cores para representar a temperatura;
if (temp < -40){
      digitalWrite(pino7, HIGH); // para os valores de if luz de led acessa, estará HIGH;
        Serial.print(F("\t  Led Marrom"));
}
if (temp >= -40 && temp < -20){
      digitalWrite(pino4, HIGH); // para os valores de if luz de led acessa, estará HIGH;
      digitalWrite(pino5, LOW); // para os valores de if luz de led apagada, estará LOW;
      digitalWrite(pino6, LOW);
        Serial.print(F("\t  Led Azul"));
}
if (temp >= -20 && temp < 0){
      digitalWrite(pino4, LOW);
      digitalWrite(pino5, HIGH);
      digitalWrite(pino6, LOW);
        Serial.print(F("\t  Led Verde"));
}
if (temp >= 0 && temp < 25){
      digitalWrite(pino4, LOW);
      digitalWrite(pino5, LOW);
      digitalWrite(pino6, HIGH);
        Serial.print(F("\t  Led Laranja"));
}
if (temp >= 25 && temp < 50){
      digitalWrite(pino4, HIGH);
      digitalWrite(pino5, HIGH);
      digitalWrite(pino6, LOW);
        Serial.print(F("\t  Led Vermelho"));
} 
if (temp >= 50 && temp <= 120){
      digitalWrite(pino4, HIGH);
      digitalWrite(pino5, HIGH);
      digitalWrite(pino6, HIGH);
        Serial.print(F("\t  Led Violeta"));
}
if (temp > 120){
      digitalWrite(pino7, HIGH); // para os valores de if luz de led acessa, estará HIGH;
        Serial.print(F("\t  Led Marrom"));
}
#endif mserial
} //fim da void loop;
      
      float func (float y){ // dividimos a equação de calculo e a variavel func esta recebendo y e a parte do calculo em variavel f;
        f = (tmax - tmin) / 2.0 * y + tmax - (tmax - tmin) / 2.0;
return f;
}
      float calculation(float temp){ // recebe o y e executa o calculo do seno;
        y = sin(w*t);
return y;  
}
